# Fritzing sketch wiring (saved by Fritzing 0.9.3b)
circuit board: 29.9268cm x 13.4684cm
breadboards: 1

parts:
  Bauteil1 = Arduino Uno (Rev3)
  S1 = Limit Switch [package="Breakout Board"]
  ENCODER1 = Rotary Encoder with switch (KY-040) [part_number=KY-040]  # not connected
  Pololu_A1 = Pololu A4988 [package=SO16]
  C1 = Capacitor Polarized [package=cpol-radial-100uf-25v]
  M1 = Stepper Motor - Bipolar
  Pololu_A2 = Pololu A4988 [package=SO16]
  C2 = Capacitor Polarized [package=cpol-radial-100uf-25v]
  M2 = Stepper Motor - Bipolar

nets (from the breadboard view):
  N1: Bauteil1.D9_PWM, Pololu_A1.STEP
  N2: Bauteil1.D10_PWM/SS, Pololu_A1.DIR
  N3: Bauteil1.D11_PWM/MOSI, S1.S
  N4: Bauteil1.GND, S1.G, Pololu_A1.GND#8, Pololu_A2.GND#8
  N5: Bauteil1.D5_PWM, Pololu_A2.STEP
  N6: Bauteil1.D6_PWM, Pololu_A2.DIR
  VDD: Bauteil1.5V, S1.V, Pololu_A1.MS3, Pololu_A1.VDD, Pololu_A2.MS3, Pololu_A2.VDD
  N7: Pololu_A1.RESET, Pololu_A1.SLEEP
  N8: Pololu_A1.1B, M1.D
  N9: Pololu_A1.1A, M1.B
  N10: Pololu_A1.2A, M1.C
  N11: Pololu_A1.2B, M1.A
  N12: Pololu_A1.GND#14, C1.+, Pololu_A2.GND#14, C2.+
  N13: Pololu_A1.VMOT, C1.-, Pololu_A2.VMOT, C2.-
  N14: Pololu_A2.RESET, Pololu_A2.SLEEP
  N15: Pololu_A2.1B, M2.D
  N16: Pololu_A2.1A, M2.B
  N17: Pololu_A2.2A, M2.C
  N18: Pololu_A2.2B, M2.A

custom parts:
  Limit Switch: Generic limit switch commonly found on 3D printers. Typical lever microswitch mounted on a PCB board with a 3 pin JST XH connector.
  Rotary Encoder with switch (KY-040): A Rotary Encoder with switch
